// Logisim project main.circ as structural Verilog
module ALU (
  input  [7:0] Data,
  input  [3:0] Control,
  input  Clk,
  input  Reset,
  output [7:0] DOUT,
  output [2:0] COZ
);

  wire and_1_out, or_1_out;
  wire [7:0] adder_1_out, register_1_q, register_2_q, subtractor_1_out;

  Register #(.trigger("falling")) register_1 (.D(Data), .en(Control[0]), .clk(Clk), .Q(register_1_q), .clr(Reset));
  Register #(.trigger("falling")) register_2 (.D(Data), .en(Control[1]), .clk(Clk), .Q(register_2_q), .clr(Reset));
  Adder adder_1 (.a(register_1_q), .b(register_2_q), .out(adder_1_out), .cout(COZ[0]));  // open: cin
  Subtractor subtractor_1 (.a(register_1_q), .b(register_2_q), .out(subtractor_1_out), .bout(COZ[1]));  // open: bin
  assign {DOUT[7:6], DOUT[6], DOUT[4:0]} = Control[2] ? adder_1_out : 8'bz;  // Controlled_Buffer controlled_buffer_1
  assign {DOUT[7:6], DOUT[6], DOUT[4:0]} = Control[3] ? subtractor_1_out : 8'bz;  // Controlled_Buffer controlled_buffer_2
  assign COZ[2] = or_1_out ? and_1_out : 1'bz;  // Controlled_Buffer controlled_buffer_3
  or or_1 (or_1_out, Control[3], Control[2]);
  and and_1 (and_1_out, ~DOUT[0], ~DOUT[1], ~DOUT[2], ~DOUT[3], ~DOUT[4], ~DOUT[6], ~DOUT[6], ~DOUT[7]);  // AND_Gate

  assign DOUT[5] = DOUT[6];
endmodule

module RegBlock (
  input  [7:0] Data,
  input  [3:0] Control,
  input  Clk,
  input  in_4,
  output [7:0] Dout
);

  wire [7:0] A_q, B_q;

  Register #(.trigger("falling")) A (.D(Data), .en(Control[0]), .clk(Clk), .Q(A_q), .clr(in_4));
  Register #(.trigger("falling")) B (.D(Data), .en(Control[1]), .clk(Clk), .Q(B_q), .clr(in_4));
  assign Dout = Control[3] ? B_q : 8'bz;  // Controlled_Buffer controlled_buffer_1
  assign Dout = Control[2] ? A_q : 8'bz;  // Controlled_Buffer controlled_buffer_2
endmodule

module CavemansCore (
  input  [7:0] in_1,
  input  in_2,
  output [7:0] out_3
);

  wire clock_1_out, controlunit_1_io, controlunit_1_ioenabled;
  wire [3:0] controlunit_1_control_alu, controlunit_1_control_regblock;
  wire [15:0] controlunit_1_address;

  Clock clock_1 (.out(clock_1_out));
  RAM #(.addrWidth(16), .databus("bidir")) ram_1 (
    .addr(controlunit_1_address), .we(controlunit_1_io), .oe(controlunit_1_ioenabled), .clk(clock_1_out),
    .data(in_1));
  ControlUnit controlunit_1 (
    .Data(in_1), .Clk(clock_1_out), .Reset(in_2), .address(controlunit_1_address),
    .Control_Regblock(controlunit_1_control_regblock), .Control_ALU(controlunit_1_control_alu),
    .IO(controlunit_1_io), .ioenabled(controlunit_1_ioenabled));  // open: Int, BS
  RegBlock regblock_1 (
    .Data(in_1), .Control(controlunit_1_control_regblock), .Clk(clock_1_out), .in_4(in_2), .Dout(in_1));
  ALU alu_1 (
    .Data(in_1), .Control(controlunit_1_control_alu), .Clk(clock_1_out), .Reset(in_2), .DOUT(in_1));  // open: COZ

  assign out_3 = in_1;
endmodule

module ControlUnit (
  input  [7:0] Data,
  input  Clk,
  input  Int,
  input  Reset,
  output [15:0] address,
  output [3:0] Control_Regblock,
  output [3:0] Control_ALU,
  output BS,
  output IO,
  output ioenabled
);

  wire and_1_out, and_2_out, and_3_out, and_4_out, and_5_out, and_6_out, and_7_out, and_8_out, and_9_out,
       and_10_out, and_11_out, and_12_out, and_13_out, and_14_out, and_15_out, controlled_buffer_3_out,
       controlled_buffer_32_out, not_1_out, not_2_out, shift_register_1_p3, shift_register_1_p5,
       shift_register_1_p11, shift_register_1_p12, shift_register_1_p13, shift_register_1_p14,
       shift_register_1_p15;
  wire [3:0] controlled_buffer_4_out;
  wire [6:0] controlled_buffer_1_out;
  wire [7:0] register_1_q;
  wire [15:0] counter_1_q, undriven;

  Register #(.trigger("falling")) register_1 (
    .D(Data), .en(shift_register_1_p11), .clk(Clk), .Q(register_1_q), .clr(Reset));
  Counter #(.max('hffff), .trigger("falling"), .width(16)) counter_1 (
    .count(controlled_buffer_32_out), .Q(counter_1_q), .up(1'b1), .clk(Clk), .clr(Reset));  // open: load, D, carry
  // Shift_Register #(.length(5), .trigger("falling")) shift_register_1: pin names not known; wires that end beside it: Clk, Int, shift_register_1_p3, Clk, shift_register_1_p5, 1'b1, 1'b0, 1'b0, 1'b0, 1'b0, shift_register_1_p11, shift_register_1_p12, shift_register_1_p13, shift_register_1_p14, shift_register_1_p15
  buf buffer_1 (shift_register_1_p3, Reset);
  and and_1 (and_1_out, ~register_1_q[0], ~register_1_q[1], ~register_1_q[2], ~register_1_q[3]);  // AND_Gate
  and and_2 (and_2_out, register_1_q[0], ~register_1_q[1], ~register_1_q[2], ~register_1_q[3]);  // AND_Gate
  buf buffer_2 (shift_register_1_p3, shift_register_1_p5);
  and and_3 (and_3_out, and_1_out, shift_register_1_p12);
  and and_4 (and_4_out, ~register_1_q[4], register_1_q[5], and_3_out);  // AND_Gate
  and and_5 (and_5_out, and_2_out, shift_register_1_p12);
  buf buffer_3 (ioenabled, shift_register_1_p11);
  buf buffer_4 (ioenabled, shift_register_1_p12);
  and and_6 (and_6_out, ~register_1_q[4], ~register_1_q[5], and_3_out);  // AND_Gate
  assign controlled_buffer_1_out[0] = and_3_out ? and_6_out : 1'bz;  // Controlled_Buffer controlled_buffer_1
  assign controlled_buffer_1_out[1] = and_3_out ? and_4_out : 1'bz;  // Controlled_Buffer controlled_buffer_2
  assign controlled_buffer_3_out = and_5_out ? and_5_out : 1'bz;  // Controlled_Buffer controlled_buffer_3
  assign {controlled_buffer_1_out[6:4], controlled_buffer_4_out[3], controlled_buffer_1_out[3], controlled_buffer_4_out[1:0]} = and_3_out ? {7{1'b0}} : 7'bz;  // Controlled_Buffer controlled_buffer_4
  buf buffer_5 (controlled_buffer_1_out[2], and_3_out);
  assign controlled_buffer_1_out = and_5_out ? {7{1'b0}} : 7'bz;  // Controlled_Buffer controlled_buffer_5
  assign controlled_buffer_4_out[0] = and_5_out ? 1'b0 : 1'bz;  // Controlled_Buffer controlled_buffer_6
  assign controlled_buffer_4_out[1] = and_5_out ? 1'b0 : 1'bz;  // Controlled_Buffer controlled_buffer_7
  assign controlled_buffer_4_out[3] = and_5_out ? 1'b0 : 1'bz;  // Controlled_Buffer controlled_buffer_8
  and and_7 (and_7_out, and_1_out, shift_register_1_p13);
  and and_8 (and_8_out, ~register_1_q[6], register_1_q[7], and_7_out);  // AND_Gate
  and and_9 (and_9_out, ~register_1_q[6], ~register_1_q[7], and_7_out);  // AND_Gate
  and and_10 (and_10_out, and_2_out, shift_register_1_p13);
  assign controlled_buffer_1_out[0] = and_7_out ? and_9_out : 1'bz;  // Controlled_Buffer controlled_buffer_9
  assign controlled_buffer_1_out[1] = and_7_out ? and_8_out : 1'bz;  // Controlled_Buffer controlled_buffer_10
  assign controlled_buffer_3_out = and_10_out ? and_10_out : 1'bz;  // Controlled_Buffer controlled_buffer_11
  assign controlled_buffer_4_out[0] = and_10_out ? 1'b1 : 1'bz;  // Controlled_Buffer controlled_buffer_12
  assign controlled_buffer_4_out[1] = and_10_out ? 1'b0 : 1'bz;  // Controlled_Buffer controlled_buffer_13
  assign controlled_buffer_4_out[3] = and_10_out ? 1'b0 : 1'bz;  // Controlled_Buffer controlled_buffer_14
  assign {controlled_buffer_1_out[6:4], controlled_buffer_4_out[3], controlled_buffer_1_out[2], controlled_buffer_4_out[1:0]} = and_7_out ? {7{1'b0}} : 7'bz;  // Controlled_Buffer controlled_buffer_15
  buf buffer_6 (controlled_buffer_1_out[3], and_7_out);
  buf buffer_7 (ioenabled, and_10_out);
  assign controlled_buffer_1_out = and_10_out ? {7{1'b0}} : 7'bz;  // Controlled_Buffer controlled_buffer_16
  and and_11 (and_11_out, and_1_out, shift_register_1_p14);
  and and_12 (and_12_out, ~register_1_q[4], ~register_1_q[5], and_11_out);  // AND_Gate
  and and_13 (and_13_out, ~register_1_q[4], register_1_q[5], and_11_out);  // AND_Gate
  and and_14 (and_14_out, and_2_out, shift_register_1_p14);
  assign controlled_buffer_3_out = and_14_out ? and_14_out : 1'bz;  // Controlled_Buffer controlled_buffer_17
  assign controlled_buffer_4_out[0] = and_11_out ? and_12_out : 1'bz;  // Controlled_Buffer controlled_buffer_18
  assign controlled_buffer_4_out[1] = and_11_out ? and_13_out : 1'bz;  // Controlled_Buffer controlled_buffer_19
  buf buffer_8 (controlled_buffer_4_out[3], and_11_out);
  assign controlled_buffer_1_out = and_14_out ? {7{1'b0}} : 7'bz;  // Controlled_Buffer controlled_buffer_20
  assign controlled_buffer_4_out[0] = and_14_out ? 1'b0 : 1'bz;  // Controlled_Buffer controlled_buffer_21
  assign controlled_buffer_4_out[1] = and_14_out ? 1'b0 : 1'bz;  // Controlled_Buffer controlled_buffer_22
  assign controlled_buffer_4_out[3] = and_14_out ? 1'b0 : 1'bz;  // Controlled_Buffer controlled_buffer_23
  assign controlled_buffer_1_out = and_11_out ? {7{1'b0}} : 7'bz;  // Controlled_Buffer controlled_buffer_24
  and and_15 (and_15_out, and_1_out, shift_register_1_p15);
  assign and_14_out = and_1_out ? and_15_out : 1'bz;  // Controlled_Buffer controlled_buffer_25
  assign controlled_buffer_3_out = and_1_out ? and_15_out : 1'bz;  // Controlled_Buffer controlled_buffer_26
  assign controlled_buffer_1_out = and_15_out ? {7{1'b0}} : 7'bz;  // Controlled_Buffer controlled_buffer_27
  assign controlled_buffer_4_out[0] = and_15_out ? 1'b0 : 1'bz;  // Controlled_Buffer controlled_buffer_28
  assign controlled_buffer_4_out[1] = and_15_out ? 1'b0 : 1'bz;  // Controlled_Buffer controlled_buffer_29
  assign controlled_buffer_4_out[3] = and_15_out ? 1'b0 : 1'bz;  // Controlled_Buffer controlled_buffer_30
  assign shift_register_1_p5 = shift_register_1_p11 ? 1'b0 : 1'bz;  // Controlled_Buffer controlled_buffer_31
  assign controlled_buffer_32_out = shift_register_1_p11 ? 1'b0 : 1'bz;  // Controlled_Buffer controlled_buffer_32
  assign shift_register_1_p5 = not_1_out ? and_14_out : 1'bz;  // Controlled_Buffer controlled_buffer_33
  assign controlled_buffer_32_out = not_1_out ? controlled_buffer_3_out : 1'bz;  // Controlled_Buffer controlled_buffer_34
  assign {IO, BS, Control_ALU, Control_Regblock} = shift_register_1_p11 ? {10{1'b0}} : 10'bz;  // Controlled_Buffer controlled_buffer_35
  not not_1 (not_1_out, shift_register_1_p11);
  assign {IO, BS, Control_ALU, Control_Regblock} = not_1_out ? {controlled_buffer_1_out[6:4], controlled_buffer_4_out[3], controlled_buffer_1_out[3:0], controlled_buffer_4_out[1:0]} : 10'bz;  // Controlled_Buffer controlled_buffer_36
  assign address = 1'b0 ? undriven : 16'bz;  // Controlled_Buffer controlled_buffer_37
  not not_2 (not_2_out, 1'b0);
  assign address = not_2_out ? counter_1_q : 16'bz;  // Controlled_Buffer controlled_buffer_38

  // Notes on the sheet:
  //   buffer_1 drives only 1 and floats otherwise
  //   buffer_2 drives only 1 and floats otherwise
  //   buffer_3 drives only 1 and floats otherwise
  //   buffer_4 drives only 1 and floats otherwise
  //   buffer_5 drives only 1 and floats otherwise
  //   buffer_6 drives only 1 and floats otherwise
  //   buffer_7 drives only 1 and floats otherwise
  //   buffer_8 drives only 1 and floats otherwise
endmodule
